// Logisim project 19CS020078085CLONE.circ as structural Verilog: 1 circuit, main circuit main
module main (
  input  [3:0] OPCODE,
  input  [3:0] Ri_ADDRESS,
  input  [3:0] Rj_ADDRESS,
  input  [3:0] Rk_ADDRESS,
  input  [15:0] IMMEDIATE,
  input  in_6,
  output [31:0] out_7,
  output [1:0] out_8,
  output [3:0] out_9,
  output [31:0] out_10,
  output s5
);

  wire ADD, ADI, AND, and_1_out, and_6_out, and_7_out, ANI, button_1_out, button_2_out, button_3_out,
       button_4_out, button_5_out, clktunnel, demultiplexer_1_out13, demultiplexer_1_out14,
       demultiplexer_1_out15, demultiplexer_2_out5, HLT, IMMSEL, IRENABLE, LOAD, MEMMUX, MOVE, MUX_Y_EN,
       MUXA_TUN, MUXB_TUN, MUXY_SEL, MVI, not_1_out, not_3_out, not_4_out, not_5_out, OR, or_1_out, or_4_out,
       or_5_out, or_6_out, or_7_out, or_8_out, or_9_out, or_10_out, or_11_out, or_12_out, or_13_out, ORI,
       PCENABLE, R1E, R2E, R3E, R4E, R5E, R6E, R7E, R8E, R9E, R10E, R11E, R12E, R13E, R14E, R15E, R16E, S3,
       S4, STORE, SUB, SUI, undriven;
  wire [2:0] counter_1_q;
  wire [3:0] ADDRESSA, ADDRESSB, ADDRESSC, OPCODETUN, Rk_ADDRESS_t;
  wire [15:0] bit_extender_1_out, IMEEDIATE_TUN, multiplexer_3_out, PC;
  wire [31:0] adder_1_out, and_2_out, bit_extender_2_out, INPUTTORGTF, MEMORYDATA, multiplexer_1_out,
       multiplexer_7_out, multiplexer_8_out, or_3_out, R1O, R2O, R3O, R4O, R5O, R6O, R7O, R8O, R9O, R10O,
       R11O, R12O, R13O, R14O, R15O, R16O, RAin, RB_q, RBin, RMSTORE, subtractor_1_out;

  and and_1 (and_1_out, R1E, not_1_out);
  not not_1 (not_1_out, IRENABLE);
  Demultiplexer #(.select(4)) demultiplexer_1 (
    .out0(MOVE), .out1(MVI), .out2(LOAD), .out3(STORE), .out4(ADD), .out5(ADI), .out6(SUB), .out7(SUI),
    .out8(AND), .out9(ANI), .out10(OR), .out11(ORI), .out12(HLT), .out13(demultiplexer_1_out13),
    .out14(demultiplexer_1_out14), .out15(demultiplexer_1_out15), .in(1'b1), .sel(OPCODETUN), .en(undriven));
  Button button_1 (.out(button_1_out));
  or or_1 (or_1_out, MOVE, LOAD, STORE, ADD, ADI, MVI);
  buf or_2 (MUXY_SEL, LOAD);  // OR_Gate
  Multiplexer #(.select(4), .width(32)) multiplexer_1 (
    .in0(R1O), .in1(R2O), .in2(R3O), .in3(R4O), .in4(R5O), .in5(R6O), .in6(R7O), .in7(R8O), .in8(R9O),
    .in9(R10O), .in10(R11O), .in11(R12O), .in12(R13O), .in13(R14O), .in14(R15O), .in15(R16O),
    .out(multiplexer_1_out), .sel(ADDRESSA), .en(MUXA_TUN));
  Adder #(.width(32)) adder_1 (.a(RAin), .b(RBin), .out(adder_1_out));  // open: cin, cout
  Subtractor #(.width(32)) subtractor_1 (.a(RAin), .b(RBin), .out(subtractor_1_out));  // open: bin, bout
  assign and_2_out = RAin & RBin;  // AND_Gate and_2, 32 bits wide
  Multiplexer #(.width(2)) multiplexer_2 (.in0(2'b00), .in1(2'b00), .out(out_8), .sel(1'b0), .en(or_1_out));
  Register #(.width(32)) R1 (.D(INPUTTORGTF), .en(and_1_out), .Q(R1O), .clk(clktunnel), .clr(button_1_out));
  Register #(.width(32)) R9 (.D(INPUTTORGTF), .en(R9E), .Q(R9O), .clk(clktunnel), .clr(button_1_out));
  Register #(.width(32)) RA (.D(multiplexer_1_out), .Q(RAin), .clk(clktunnel), .clr(button_2_out));  // open: en
  Button button_2 (.out(button_2_out));
  assign or_3_out = RAin | RBin;  // OR_Gate or_3, 32 bits wide
  Multiplexer #(.width(16)) multiplexer_3 (
    .in0(PC), .in1(bit_extender_1_out), .out(multiplexer_3_out), .sel(MEMMUX));  // open: en
  Bit_Extender #(.in_width(32)) bit_extender_1 (.in(out_10), .out(bit_extender_1_out));
  or or_4 (or_4_out, MOVE, LOAD, STORE, ADD, ADI, SUB, SUI, AND, ANI, OR, ORI);
  or or_5 (or_5_out, MOVE, LOAD, STORE, ADD, ADI, SUB, SUI, AND, ANI, OR, ORI);
  Multiplexer #(.width(4)) multiplexer_4 (.in0(4'b0000), .in1(out_9), .out(ADDRESSA), .sel(1'b1), .en(or_4_out));
  or or_6 (or_6_out, SUB, SUI);
  or or_7 (or_7_out, LOAD, STORE);
  // Probe on {IMMEDIATE, Rk_ADDRESS, Rj_ADDRESS, Ri_ADDRESS, OPCODE}
  Register #(.width(32)) R2 (.D(INPUTTORGTF), .en(R2E), .Q(R2O), .clk(clktunnel), .clr(button_1_out));
  Register #(.width(32)) R10 (.D(INPUTTORGTF), .en(R10E), .Q(R10O), .clk(clktunnel), .clr(button_1_out));
  Multiplexer #(.select(2), .width(32)) multiplexer_5 (
    .in0(adder_1_out), .in1(subtractor_1_out), .in2(and_2_out), .in3(or_3_out), .out(out_7), .sel(out_8));  // open: en
  or or_8 (or_8_out, IRENABLE, LOAD);
  and and_3 (MUXA_TUN, PCENABLE, or_5_out);
  Multiplexer #(.width(2)) multiplexer_6 (.in0(2'b01), .in1(2'b00), .out(out_8), .sel(1'b0), .en(or_6_out));
  or or_9 (or_9_out, s5, S4, S3);
  Register #(.width(32)) R3 (.D(INPUTTORGTF), .en(R3E), .Q(R3O), .clk(clktunnel), .clr(button_1_out));
  Register #(.width(32)) R11 (.D(INPUTTORGTF), .en(R11E), .Q(R11O), .clk(clktunnel), .clr(button_1_out));
  Register #(.width(32)) RZ (.D(out_7), .Q(out_10), .clk(clktunnel), .clr(button_3_out));  // open: en
  Multiplexer #(.width(32)) multiplexer_7 (
    .in0(out_10), .in1(MEMORYDATA), .out(multiplexer_7_out), .sel(MUXY_SEL), .en(MUX_Y_EN));
  RAM #(.addrWidth(16), .dataWidth(32), .bus("separate")) ram_1 (
    .addr(multiplexer_3_out), .din(RMSTORE), .data(MEMORYDATA), .str(STORE), .clk(clktunnel), .ld(or_8_out),
    .clr(in_6));  // open: sel
  Demultiplexer #(.select(3)) demultiplexer_2 (
    .out0(IRENABLE), .out1(PCENABLE), .out2(S3), .out3(S4), .out4(s5), .out5(demultiplexer_2_out5),
    .in(1'b1), .sel(counter_1_q));  // open: out6, out7, en
  Counter #(.width(3), .max('h7)) counter_1 (
    .Q(counter_1_q), .clk(clktunnel), .clr(demultiplexer_2_out5));  // open: load, D, count, carry
  and and_4 (MEMMUX, or_9_out, or_7_out);
  Register #(.width(32)) RY (.D(multiplexer_7_out), .Q(INPUTTORGTF), .clk(clktunnel), .clr(button_3_out));  // open: en
  Button button_3 (.out(button_3_out));
  Register #(.width(32)) R4 (.D(INPUTTORGTF), .en(R4E), .Q(R4O), .clk(clktunnel), .clr(button_1_out));
  Register #(.width(32)) R12 (.D(INPUTTORGTF), .en(R12E), .Q(R12O), .clk(clktunnel), .clr(button_1_out));
  Register #(.width(32)) register_1 (
    .D(MEMORYDATA), .en(IRENABLE), .Q({IMEEDIATE_TUN, Rk_ADDRESS_t, out_9, ADDRESSC, OPCODETUN}),
    .clk(clktunnel), .clr(button_4_out));
  Button button_4 (.out(button_4_out));
  or or_10 (or_10_out, ADD, SUB, AND, OR, STORE);
  or or_11 (or_11_out, ADD, SUB, AND, OR);
  and and_5 (MUXB_TUN, PCENABLE, or_10_out);
  or or_12 (or_12_out, AND, ANI);
  not not_2 (MUX_Y_EN, STORE);
  Register #(.width(32)) R5 (.D(INPUTTORGTF), .en(R5E), .Q(R5O), .clk(clktunnel), .clr(button_1_out));
  Register #(.width(32)) R13 (.D(INPUTTORGTF), .en(R13E), .Q(R13O), .clk(clktunnel), .clr(button_1_out));
  Multiplexer #(.select(4), .width(32)) multiplexer_8 (
    .in0(R1O), .in1(R2O), .in2(R3O), .in3(R4O), .in4(R5O), .in5(R6O), .in6(R7O), .in7(R8O), .in8(R9O),
    .in9(R10O), .in10(R11O), .in11(R12O), .in12(R13O), .in13(R14O), .in14(R15O), .in15(R16O),
    .out(multiplexer_8_out), .sel(ADDRESSB), .en(MUXB_TUN));
  not not_3 (not_3_out, HLT);
  Multiplexer #(.width(4)) multiplexer_9 (
    .in0(4'b0000), .in1(Rk_ADDRESS_t), .out(ADDRESSB), .sel(1'b1), .en(or_11_out));
  Multiplexer #(.width(2)) multiplexer_10 (.in0(2'b10), .in1(2'b00), .out(out_8), .sel(1'b0), .en(or_12_out));
  Register #(.width(32)) R6 (.D(INPUTTORGTF), .en(R6E), .Q(R6O), .clk(clktunnel), .clr(button_1_out));
  Register #(.width(32)) RB (.D(multiplexer_8_out), .Q(RB_q), .clk(clktunnel), .clr(button_2_out));  // open: en
  and and_6 (and_6_out, PCENABLE, not_3_out);
  Clock clk (.out(clktunnel));
  Register #(.width(32)) R14 (.D(INPUTTORGTF), .en(R14E), .Q(R14O), .clk(clktunnel), .clr(button_1_out));
  Multiplexer #(.width(32)) multiplexer_11 (
    .in0(RB_q), .in1(bit_extender_2_out), .out(RBin), .sel(IMMSEL));  // open: en
  or or_13 (or_13_out, OR, ORI);
  Register #(.width(32)) R7 (.D(INPUTTORGTF), .en(R7E), .Q(R7O), .clk(clktunnel), .clr(button_1_out));
  Register #(.width(32)) R15 (.D(INPUTTORGTF), .en(R15E), .Q(R15O), .clk(clktunnel), .clr(button_1_out));
  assign bit_extender_2_out = {{16{1'b0}}, IMEEDIATE_TUN};  // Bit_Extender bit_extender_2
  Counter #(.width(16), .max('hffff)) counter_2 (
    .count(and_6_out), .Q(PC), .clk(clktunnel), .clr(button_5_out));  // open: load, D, carry
  Multiplexer #(.width(2)) multiplexer_12 (.in0(2'b11), .in1(2'b00), .out(out_8), .sel(1'b0), .en(or_13_out));
  Button button_5 (.out(button_5_out));
  Multiplexer #(.width(4)) multiplexer_13 (.in0(4'b0000), .in1(ADDRESSC), .out(ADDRESSB), .sel(1'b1), .en(STORE));
  or or_14 (IMMSEL, LOAD, MOVE, MVI, ADI, SUI, ANI, ORI, STORE);
  Register #(.width(32)) R8 (.D(INPUTTORGTF), .en(R8E), .Q(R8O), .clk(clktunnel), .clr(button_1_out));
  Register #(.width(32)) R16 (.D(INPUTTORGTF), .en(R16E), .Q(R16O), .clk(clktunnel), .clr(button_1_out));
  and and_7 (and_7_out, 1'b1, not_4_out, not_5_out);
  Demultiplexer #(.select(4)) demultiplexer_3 (
    .out0(R1E), .out1(R2E), .out2(R3E), .out3(R4E), .out4(R5E), .out5(R6E), .out6(R7E), .out7(R8E),
    .out8(R9E), .out9(R10E), .out10(R11E), .out11(R12E), .out12(R13E), .out13(R14E), .out14(R15E),
    .out15(R16E), .in(and_7_out), .sel(ADDRESSC));  // open: en
  Register #(.width(32)) RM (.D(RB_q), .en(STORE), .Q(RMSTORE), .clk(clktunnel));  // open: clr
  not not_4 (not_4_out, STORE);
  not not_5 (not_5_out, HLT);

  // Other names for the same wires on the sheet: ALUDMX[1:0] = out_8; MEMORYADDRESS[31:0] = out_10;
  //   Ri_ADDRESS_t[3:0] = ADDRESSC; Rj_ADDRESS_t[3:0] = out_9; RZin[31:0] = out_7; S2 = PCENABLE

  // Notes on the sheet:
  //   HEXCONVERTOR
  //   --------------ALU----------
  //   ----------------------------------------------------FIVE STAGE PIPE LINE---------------------------------------
  //   -----------------------------------MEMORY----------------------------------
  //   !!NOTE THIS IS JUST FOR CONVERSION PURPOSE 
  //   AFTER Converting we have to enter it into memory
  //   --------------------------------CONTROLSIGNAL-----------------------------------------------
  //   ----------------PC---------
endmodule
